# Fritzing sketch Untitled_Sketch (saved by Fritzing 0.9.3b)

parts:
  Composant2 = Arduino Uno (Rev3)
  Composant3 = DFROBOT Hx711
  Load_Sensor1 = Load Sensor

nets:
  N1: Composant2.A2, Composant3.DOUT
  5V: Composant2.A3, Composant2.5V, Composant3.SCK, Composant3.VCC
  GND: Composant2.GND, Composant3.GND
  N2: Composant3.E+, Load_Sensor1.E+
  N3: Composant3.S+, Load_Sensor1.S+
  N4: Composant3.S-, Load_Sensor1.S-
  N5: Composant3.E-, Load_Sensor1.E-
